// Logisim project LC3CPU.circ as structural Verilog: 9 circuits, main circuit Computer
module Computer (
);

  wire clock_1_out, MemoryWrite;
  wire [2:0] cpu_1_nzp;
  wire [15:0] cpu_1_r0, cpu_1_r1, cpu_1_r2, cpu_1_r3, cpu_1_r4, cpu_1_r5, cpu_1_r6, cpu_1_r7, MemoryAddress,
       MemoryOut, multiplexer_1_out, PC, ram_1_dout;

  Clock clock_1 (.out(clock_1_out));
  Multiplexer #(.width(16)) multiplexer_1 (.in0(PC), .in1(MemoryAddress), .out(multiplexer_1_out), .sel(clock_1_out));
  RAM #(.addrWidth(16), .dataWidth(16), .enables("line"), .trigger("falling")) ram_1 (
    .addr(multiplexer_1_out), .we(MemoryWrite), .clk(clock_1_out), .din(MemoryOut), .dout(ram_1_dout));
  CPU cpu_1 (
    .MemoryIn(ram_1_dout), .clock(clock_1_out), .R0(cpu_1_r0), .R1(cpu_1_r1), .R2(cpu_1_r2), .R3(cpu_1_r3),
    .R4(cpu_1_r4), .R5(cpu_1_r5), .R6(cpu_1_r6), .R7(cpu_1_r7), .NZP(cpu_1_nzp), .PC(PC),
    .MemoryAddress(MemoryAddress), .MemoryOut(MemoryOut), .MemoryWrite(MemoryWrite));
  // Probe on MemoryWrite
  // Probe on cpu_1_r0
  // Probe on cpu_1_r1
  // Probe on cpu_1_r2
  // Probe on cpu_1_r3
  // Probe on cpu_1_r4
  // Probe on cpu_1_r5
  // Probe on cpu_1_r6
  // Probe on cpu_1_r7
  // Probe on cpu_1_nzp
  // Probe on MemoryOut
  // Probe on MemoryAddress
  // Probe on PC

  // Notes on the sheet:
  //   When the clock is low CPU fetches.
  //   When the clock is high the CPU executes.
  //   A better design would have the CPU work in phases.
endmodule

module CPU (
  input  [15:0] MemoryIn,
  input  clock,
  output [15:0] R0,
  output [15:0] R1,
  output [15:0] R2,
  output [15:0] R3,
  output [15:0] R4,
  output [15:0] R5,
  output [15:0] R6,
  output [15:0] R7,
  output [2:0] NZP,
  output [15:0] PC,
  output [15:0] MemoryAddress,
  output [15:0] MemoryOut,
  output MemoryWrite
);

  wire control_1_alu_add, control_1_alu_and, control_1_alu_not, control_1_halt, control_1_we, Jump, or_1_out;
  wire [2:0] control_1_drnumber, control_1_sr1number, control_1_sr2number;
  wire [15:0] control_1_data, control_1_operand1, control_1_operand2, IR_q, PC_Plus_1, SR1, SR2;

  Register #(.width(16)) IR (.D(MemoryIn), .clk(or_1_out), .Q(IR_q));  // open: en, clr
  Control control_1 (
    .Instruction(IR_q), .NZP(NZP), .SR1(SR1), .SR2(SR2), .PC(PC_Plus_1), .Result(MemoryAddress),
    .Memory(MemoryIn), .DRnumber(control_1_drnumber), .SR1number(control_1_sr1number),
    .SR2number(control_1_sr2number), .ALU_NOT(control_1_alu_not), .ALU_AND(control_1_alu_and),
    .ALU_ADD(control_1_alu_add), .Operand1(control_1_operand1), .Operand2(control_1_operand2),
    .Data(control_1_data), .WE(control_1_we), .Halt(control_1_halt), .MemoryWrite(MemoryWrite), .Jump(Jump));
  or or_1 (or_1_out, clock, control_1_halt);
  // Probe on MemoryAddress
  ALU alu_1 (
    .Operand1(control_1_operand1), .Operand2(control_1_operand2), .ALU_Add(control_1_alu_add),
    .ALU_And(control_1_alu_and), .ALU_Not(control_1_alu_not), .Result(MemoryAddress));
  RegisterFile registerfile_1 (
    .Data(control_1_data), .WE(control_1_we), .DRnumber(control_1_drnumber), .SR1number(control_1_sr1number),
    .SR2number(control_1_sr2number), .Clock(or_1_out), .R0(R0), .R1(R1), .R2(R2), .R3(R3), .R4(R4), .R5(R5),
    .R6(R6), .R7(R7), .DR(MemoryOut), .SR1(SR1), .SR2(SR2));
  Status status_1 (.Data(control_1_data), .WE(control_1_we), .Clock(or_1_out), .P(NZP[0]), .Z(NZP[1]), .N(NZP[2]));
  ProgramCounter programcounter_1 (
    .JumpLocation(MemoryAddress), .Jump(Jump), .Clock(or_1_out), .PC(PC), .PC_Plus_1(PC_Plus_1));

  // Other names for the same wires on the sheet: DR[15:0] = MemoryOut; Result[15:0] = MemoryAddress
endmodule

module ProgramCounter (
  input  [15:0] JumpLocation,
  input  Jump,
  input  Clock,
  output [15:0] PC,
  output [15:0] PC_Plus_1
);

  wire [15:0] multiplexer_1_out;

  Adder #(.width(16)) adder_1 (.a(PC), .b(16'h1), .out(PC_Plus_1));  // open: cin, cout
  Multiplexer #(.width(16)) multiplexer_1 (.in0(PC_Plus_1), .in1(JumpLocation), .out(multiplexer_1_out), .sel(Jump));
  Register #(.trigger("falling"), .width(16)) register_1 (.D(multiplexer_1_out), .clk(Clock), .Q(PC));  // open: en, clr
endmodule

module RegisterFile (
  input  [15:0] Data,
  input  WE,
  input  [2:0] DRnumber,
  input  [2:0] SR1number,
  input  [2:0] SR2number,
  input  Clock,
  output [15:0] R0,
  output [15:0] R1,
  output [15:0] R2,
  output [15:0] R3,
  output [15:0] R4,
  output [15:0] R5,
  output [15:0] R6,
  output [15:0] R7,
  output [15:0] DR,
  output [15:0] SR1,
  output [15:0] SR2
);

  wire demultiplexer_1_out0, demultiplexer_1_out1, demultiplexer_1_out2, demultiplexer_1_out3,
       demultiplexer_1_out4, demultiplexer_1_out5, demultiplexer_1_out6, demultiplexer_1_out7;

  Demultiplexer #(.select(3)) demultiplexer_1 (
    .out0(demultiplexer_1_out0), .out1(demultiplexer_1_out1), .out2(demultiplexer_1_out2),
    .out3(demultiplexer_1_out3), .out4(demultiplexer_1_out4), .out5(demultiplexer_1_out5),
    .out6(demultiplexer_1_out6), .out7(demultiplexer_1_out7), .in(WE), .sel(DRnumber));
  Register #(.trigger("falling"), .width(16)) register_1 (
    .D(Data), .en(demultiplexer_1_out0), .clk(Clock), .Q(R0));  // open: clr
  Register #(.trigger("falling"), .width(16)) register_2 (
    .D(Data), .en(demultiplexer_1_out1), .clk(Clock), .Q(R1));  // open: clr
  Register #(.trigger("falling"), .width(16)) register_3 (
    .D(Data), .en(demultiplexer_1_out2), .clk(Clock), .Q(R2));  // open: clr
  Register #(.trigger("falling"), .width(16)) register_4 (
    .D(Data), .en(demultiplexer_1_out3), .clk(Clock), .Q(R3));  // open: clr
  Register #(.trigger("falling"), .width(16)) register_5 (
    .D(Data), .en(demultiplexer_1_out4), .clk(Clock), .Q(R4));  // open: clr
  Register #(.trigger("falling"), .width(16)) register_6 (
    .D(Data), .en(demultiplexer_1_out5), .clk(Clock), .Q(R5));  // open: clr
  Register #(.trigger("falling"), .width(16)) register_7 (
    .D(Data), .en(demultiplexer_1_out6), .clk(Clock), .Q(R6));  // open: clr
  Register #(.trigger("falling"), .width(16)) register_8 (
    .D(Data), .en(demultiplexer_1_out7), .clk(Clock), .Q(R7));  // open: clr
  Multiplexer #(.select(3), .width(16)) multiplexer_1 (
    .in0(R0), .in1(R1), .in2(R2), .in3(R3), .in4(R4), .in5(R5), .in6(R6), .in7(R7), .out(DR), .sel(DRnumber));
  Multiplexer #(.select(3), .width(16)) multiplexer_2 (
    .in0(R0), .in1(R1), .in2(R2), .in3(R3), .in4(R4), .in5(R5), .in6(R6), .in7(R7), .out(SR1), .sel(SR1number));
  Multiplexer #(.select(3), .width(16)) multiplexer_3 (
    .in0(R0), .in1(R1), .in2(R2), .in3(R3), .in4(R4), .in5(R5), .in6(R6), .in7(R7), .out(SR2), .sel(SR2number));
endmodule

module Status (
  input  [15:0] Data,
  input  WE,
  input  Clock,
  output P,
  output Z,
  output N
);

  wire and_1_out, nor_1_out, not_1_out, or_1_out, zero_q;

  or or_1 (or_1_out, Data[0], Data[1], Data[2], Data[3], Data[4], Data[5], Data[6], Data[7], Data[8], Data[9], Data[10], Data[11], Data[12], Data[13], Data[14], Data[15]);
  and and_1 (and_1_out, or_1_out, ~Data[15], WE);  // AND_Gate
  not not_1 (not_1_out, or_1_out);
  Register #(.trigger("falling"), .width(1)) positive (.D(and_1_out), .en(WE), .clk(Clock), .Q(P));  // open: clr
  Register #(.trigger("falling"), .width(1)) zero (.D(not_1_out), .en(WE), .clk(Clock), .Q(zero_q));  // open: clr
  Register #(.trigger("falling"), .width(1)) negative (.D(Data[15]), .en(WE), .clk(Clock), .Q(N));  // open: clr
  or or_2 (Z, zero_q, nor_1_out);
  nor nor_1 (nor_1_out, P, N);
endmodule

module ALU (
  input  [15:0] Operand1,
  input  [15:0] Operand2,
  input  ALU_Add,
  input  ALU_And,
  input  ALU_Not,
  output [15:0] Result
);

  wire [15:0] adder_1_out, and_1_out, multiplexer_1_out, multiplexer_2_out, not_1_out;

  Adder #(.width(16)) adder_1 (.a(Operand1), .b(Operand2), .out(adder_1_out));  // open: cin, cout
  assign and_1_out = Operand1 & Operand2;  // AND_Gate and_1, 16 bits wide
  Multiplexer #(.width(16)) multiplexer_1 (.in0(Operand1), .in1(adder_1_out), .out(multiplexer_1_out), .sel(ALU_Add));
  Multiplexer #(.width(16)) multiplexer_2 (
    .in0(multiplexer_1_out), .in1(and_1_out), .out(multiplexer_2_out), .sel(ALU_And));
  assign not_1_out = ~Operand1;  // NOT_Gate not_1, 16 bits wide
  Multiplexer #(.width(16)) multiplexer_3 (.in0(multiplexer_2_out), .in1(not_1_out), .out(Result), .sel(ALU_Not));

  // Notes on the sheet:
  //   mux a
  //   mux b
endmodule

module JumpDecoder (
  input  [2:0] NZP_Status,
  input  [2:0] NZP_Intruction,
  input  BRop,
  input  JMPop,
  output Jump
);

  wire and_2_out, or_1_out;
  wire [2:0] and_1_out;

  assign and_1_out = NZP_Status & NZP_Intruction;  // AND_Gate and_1, 3 bits wide
  or or_1 (or_1_out, and_1_out[0], and_1_out[1], and_1_out[2]);
  and and_2 (and_2_out, or_1_out, BRop);
  or or_2 (Jump, and_2_out, JMPop);
endmodule

module InstructionDecoder (
  input  [15:0] instruction,
  output [2:0] DRnumber,
  output [2:0] SR1number,
  output [2:0] SR2number,
  output [15:0] imm5,
  output [15:0] PCoffset9,
  output [15:0] offset6,
  output ADDop,
  output ADDIop,
  output ANDop,
  output ANDIop,
  output BRop,
  output JMPop,
  output LDop,
  output LDRop,
  output LEAop,
  output NOTop,
  output STop,
  output STRop,
  output HALTop
);

  wire decoder_1_out1, decoder_1_out5;

  Decoder #(.enable("false"), .select(4)) decoder_1 (
    .out0(BRop), .out1(decoder_1_out1), .out2(LDop), .out3(STop), .out5(decoder_1_out5), .out6(LDRop),
    .out7(STRop), .out9(NOTop), .out12(JMPop), .out14(LEAop), .out15(HALTop), .sel(instruction[15:12]));  // open: out4, out8, out10, out11, out13
  Comparator #(.width(16)) comparator_1 (.a(instruction), .b(16'hf025), .eq(HALTop));  // open: gt, lt
  and and_1 (ADDIop, decoder_1_out1, instruction[5]);
  and and_2 (ADDop, ~instruction[5], decoder_1_out1);  // AND_Gate
  and and_3 (ANDop, ~instruction[5], decoder_1_out5);  // AND_Gate
  and and_4 (ANDIop, instruction[5], decoder_1_out5);
  assign imm5 = {{11{instruction[4]}}, instruction[4:0]};  // Bit_Extender bit_extender_1
  assign PCoffset9 = {{7{instruction[8]}}, instruction[8:0]};  // Bit_Extender bit_extender_2
  assign offset6 = {{10{instruction[5]}}, instruction[5:0]};  // Bit_Extender bit_extender_3

  assign DRnumber = instruction[11:9];
  assign SR1number = instruction[8:6];
  assign SR2number = instruction[2:0];
endmodule

module Control (
  input  [15:0] Instruction,
  input  [2:0] NZP,
  input  [15:0] SR1,
  input  [15:0] SR2,
  input  [15:0] PC,
  input  [15:0] Result,
  input  [15:0] Memory,
  output [2:0] DRnumber,
  output [2:0] SR1number,
  output [2:0] SR2number,
  output ALU_NOT,
  output ALU_AND,
  output ALU_ADD,
  output [15:0] Operand1,
  output [15:0] Operand2,
  output [15:0] Data,
  output WE,
  output Halt,
  output MemoryWrite,
  output Jump
);

  wire instructiondecoder_1_addiop, instructiondecoder_1_addop, instructiondecoder_1_andiop,
       instructiondecoder_1_andop, instructiondecoder_1_brop, instructiondecoder_1_jmpop,
       instructiondecoder_1_ldop, instructiondecoder_1_ldrop, instructiondecoder_1_leaop,
       instructiondecoder_1_stop, instructiondecoder_1_strop, or_4_out, or_5_out, or_6_out, or_7_out,
       or_8_out;
  wire [1:0] pull_resistor_1_node;
  wire [15:0] IMM5, offset6, PCoffset9;

  InstructionDecoder instructiondecoder_1 (
    .instruction(Instruction), .DRnumber(DRnumber), .SR1number(SR1number), .SR2number(SR2number),
    .imm5(IMM5), .PCoffset9(PCoffset9), .offset6(offset6), .ADDop(instructiondecoder_1_addop),
    .ADDIop(instructiondecoder_1_addiop), .ANDop(instructiondecoder_1_andop),
    .ANDIop(instructiondecoder_1_andiop), .BRop(instructiondecoder_1_brop),
    .JMPop(instructiondecoder_1_jmpop), .LDop(instructiondecoder_1_ldop), .LDRop(instructiondecoder_1_ldrop),
    .LEAop(instructiondecoder_1_leaop), .NOTop(ALU_NOT), .STop(instructiondecoder_1_stop),
    .STRop(instructiondecoder_1_strop), .HALTop(Halt));
  or or_1 (ALU_AND, instructiondecoder_1_andop, instructiondecoder_1_andiop);
  or or_2 (ALU_ADD, instructiondecoder_1_ldrop, instructiondecoder_1_addop, instructiondecoder_1_addiop, instructiondecoder_1_brop, instructiondecoder_1_jmpop, instructiondecoder_1_leaop, instructiondecoder_1_stop, instructiondecoder_1_strop, instructiondecoder_1_ldop);
  or or_3 (MemoryWrite, instructiondecoder_1_stop, instructiondecoder_1_strop);
  JumpDecoder jumpdecoder_1 (
    .NZP_Status(NZP), .NZP_Intruction(DRnumber), .BRop(instructiondecoder_1_brop),
    .JMPop(instructiondecoder_1_jmpop), .Jump(Jump));
  or or_4 (or_4_out, instructiondecoder_1_ldrop, instructiondecoder_1_ldop);
  Multiplexer #(.width(16)) multiplexer_1 (.in0(Result), .in1(Memory), .out(Data), .sel(or_4_out));
  or or_5 (or_5_out, instructiondecoder_1_brop, instructiondecoder_1_ldop, instructiondecoder_1_stop, instructiondecoder_1_leaop);
  Multiplexer #(.width(16)) multiplexer_2 (.in0(SR1), .in1(PC), .out(Operand1), .sel(or_5_out));
  or or_6 (or_6_out, instructiondecoder_1_andop, instructiondecoder_1_ldrop);
  or or_7 (or_7_out, instructiondecoder_1_andiop, instructiondecoder_1_addiop);
  or or_8 (or_8_out, instructiondecoder_1_ldrop, instructiondecoder_1_strop, instructiondecoder_1_jmpop);
  or or_9 (WE, instructiondecoder_1_addop, instructiondecoder_1_addiop, instructiondecoder_1_andop, instructiondecoder_1_andiop, instructiondecoder_1_ldop, instructiondecoder_1_ldrop, instructiondecoder_1_leaop, ALU_NOT);
  Pull_Resistor pull_resistor_1 (.node(pull_resistor_1_node));
  Priority_Encoder #(.select(2)) priority_encoder_1 (
    .in0(or_6_out), .in1(or_7_out), .in2(or_8_out), .in3(or_5_out), .out(pull_resistor_1_node));  // open: gs, en_out, en_in
  // Probe on pull_resistor_1_node
  Multiplexer #(.select(2), .width(16)) multiplexer_3 (
    .in0(SR2), .in1(IMM5), .in2(offset6), .in3(PCoffset9), .out(Operand2), .sel(pull_resistor_1_node));

  // Other names for the same wires on the sheet: OPERAND1_t[15:0] = Operand2
endmodule
